// Logisim project control-logic.circ as structural Verilog: 1 circuit, main circuit control_logic
module control_logic (
  input  [31:0] inst,
  input  BrEq,
  input  BrLt,
  output PCSel,
  output RegWEn,
  output [2:0] ImmSel,
  output BrUn,
  output ASel,
  output BSel,
  output [3:0] ALUSel,
  output MemRW,
  output [1:0] WBSel,
  output CSRSel,
  output CSRWen
);

  wire and_1_out, and_2_out, comparator_8_eq, comparator_9_eq, comparator_12_eq, I, is_jalr, is_load, is_lui,
       multiplexer_6_out, NOP, not_1_out, not_3_out, or_7_out, or_8_out, R, SB, SBPCSel, U, UJ;
  wire [1:0] multiplexer_2_out;
  wire [3:0] IALU, multiplexer_1_out, multiplexer_3_out, multiplexer_7_out, RALU;
  wire [3:3] and_3_out;

  or or_1 (ImmSel[1], MemRW, CSRWen, SB);
  and and_1 (and_1_out, U, not_1_out);
  not not_1 (not_1_out, inst[5]);
  not not_2 (BSel, R);
  and and_2 (and_2_out, SBPCSel, SB);
  or or_2 (RegWEn, R, I, U, UJ);
  or or_3 (ImmSel[0], I, SB, UJ);
  or or_4 (ImmSel[2], U, CSRWen, UJ);
  or or_5 (ASel, and_1_out, SB, UJ);
  Comparator #(.mode("unsigned"), .width(7)) comparator_1 (.a(inst[6:0]), .b(7'b0110011), .eq(R));  // open: gt, lt
  Comparator #(.mode("unsigned"), .width(7)) comparator_2 (.a(inst[6:0]), .b(7'b0100011), .eq(MemRW));  // open: gt, lt
  Comparator #(.mode("unsigned"), .width(7)) comparator_3 (.a(inst[6:0]), .b(7'b1101111), .eq(UJ));  // open: gt, lt
  Comparator #(.mode("unsigned"), .width(7)) comparator_4 (.a(inst[6:0]), .b(7'b1100011), .eq(SB));  // open: gt, lt
  Comparator #(.mode("unsigned"), .width(7)) comparator_5 (.a(inst[6:0]), .b(7'b0110111), .eq(is_lui));  // open: gt, lt
  nor nor_1 (I, CSRWen, R, MemRW, NOP, SB, U, UJ);
  or or_6 (PCSel, and_2_out, is_jalr, UJ);
  or or_7 (or_7_out, is_lui, CSRWen);
  not not_3 (not_3_out, is_load);
  Comparator #(.mode("unsigned"), .width(7)) comparator_6 (
    .a(inst[6:0]), .b(7'b1100111), .eq(is_jalr));  // open: gt, lt
  Comparator #(.mode("unsigned"), .width(7)) comparator_7 (
    .a(inst[6:0]), .b(7'b0000011), .eq(is_load));  // open: gt, lt
  Comparator #(.width(7)) comparator_8 (.a(7'b0010111), .b(inst[6:0]), .eq(comparator_8_eq));  // open: gt, lt
  Comparator #(.mode("unsigned"), .width(7)) comparator_9 (
    .a(inst[6:0]), .b(7'b0110111), .eq(comparator_9_eq));  // open: gt, lt
  Comparator #(.mode("unsigned"), .width(7)) comparator_10 (
    .a(inst[6:0]), .b(7'b1110011), .eq(CSRWen));  // open: gt, lt
  Multiplexer #(.enable("false"), .width(4)) multiplexer_1 (
    .in0(4'b0000), .in1(4'b1111), .out(multiplexer_1_out), .sel(or_7_out));
  Multiplexer #(.enable("false"), .width(2)) multiplexer_2 (
    .in0(2'b00), .in1(2'b01), .out(multiplexer_2_out), .sel(not_3_out));
  or or_8 (or_8_out, is_jalr, UJ);
  or or_9 (U, comparator_8_eq, comparator_9_eq);
  Multiplexer #(.enable("false"), .width(4)) multiplexer_3 (
    .in0(multiplexer_1_out), .in1(IALU), .out(multiplexer_3_out), .sel(I));
  Multiplexer #(.enable("false"), .width(2)) multiplexer_4 (
    .in0(multiplexer_2_out), .in1(2'b10), .out(WBSel), .sel(or_8_out));
  Multiplexer #(.enable("false"), .width(4)) multiplexer_5 (.in0(multiplexer_3_out), .in1(RALU), .out(ALUSel), .sel(R));
  Comparator #(.mode("unsigned"), .width(7)) comparator_11 (.a(inst[6:0]), .b({7{1'b0}}), .eq(NOP));  // open: gt, lt
  Multiplexer #(.enable("false")) multiplexer_6 (.in0(BrEq), .in1(BrLt), .out(multiplexer_6_out), .sel(inst[14]));
  Comparator #(.width(3)) comparator_12 (.a(3'b101), .b(inst[14:12]), .eq(comparator_12_eq));  // open: gt, lt
  Multiplexer #(.enable("false"), .width(4)) multiplexer_7 (
    .in0(4'b1100), .in1(4'b1101), .out(multiplexer_7_out), .sel(inst[14]));
  and and_3 (and_3_out[3], comparator_12_eq, inst[30]);
  xor xor_1 (SBPCSel, multiplexer_6_out, inst[12]);
  Multiplexer #(.enable("false"), .width(4)) multiplexer_8 (
    .in0({inst[25], inst[14:12]}), .in1(multiplexer_7_out), .out(RALU), .sel(inst[30]));
  Multiplexer #(.enable("false"), .width(4)) multiplexer_9 (
    .in0({and_3_out[3], inst[14:12]}), .in1(4'b0000), .out(IALU), .sel(is_load));

  assign BrUn = inst[13];
  assign CSRSel = inst[14];

  // Other names for the same wires on the sheet: funct7[6:0] = inst[31:25]; funct7bit0 = inst[25];
  //   funct3[2:0] = inst[14:12]; funct3bit0 = inst[12]; funct3bit1 = inst[13]; funct3bit2 = inst[14]; CSR = CSRWen;
  //   opcode[6:0] = inst[6:0]; funct7bit5 = inst[30]; S = MemRW

  // Notes on the sheet:
  //   INPUTS to your circuit
  //   DON'T CHANGE THE LOCATIONS OF THE INPUTS AND OUTPUTS!
  //   OUTPUT from your circuit
endmodule
