// Logisim project cpu.circ as structural Verilog: 1 circuit, main circuit cpu
module cpu (
  input  clk,
  input  [31:0] INSTRUCTION,
  input  [31:0] READ_DATA,
  output [31:0] WRITE_ADDRESS,
  output [31:0] PROGRAM_COUNTER,
  output [31:0] ra,
  output [31:0] sp,
  output [31:0] t0,
  output [31:0] t1,
  output [31:0] t2,
  output [31:0] s0,
  output [31:0] s1,
  output [31:0] a0,
  output [31:0] tohost,
  output [3:0] WRITE_ENABLE,
  output [31:0] WRITE_DATA
);

  wire branch_comp_1_breq, branch_comp_1_brlt, control_logic_1_asel, control_logic_1_brun,
       control_logic_1_bsel, control_logic_1_csrsel, control_logic_1_csrwen, control_logic_1_memrw,
       control_logic_1_regwen, LastPCSel, PCSel;
  wire [1:0] WBSel;
  wire [2:0] control_logic_1_immsel;
  wire [3:0] control_logic_1_alusel, multiplexer_7_out, shifter_1_out;
  wire [7:0] multiplexer_10_out;
  wire [15:0] multiplexer_9_out;
  wire [31:0] adder_2_out, bit_extender_1_out, bit_extender_2_out, imm_gen_1_imm, LastALUResult,
       multiplexer_1_out, multiplexer_2_out, multiplexer_3_out, multiplexer_4_out, multiplexer_5_out,
       multiplexer_6_out, PC4, PINST, PipelinePC, ReadResult, rs1, rs2;

  Multiplexer #(.enable("false"), .width(32)) multiplexer_1 (
    .in0(INSTRUCTION), .in1({32{1'b0}}), .out(multiplexer_1_out), .sel(PCSel));
  Register #(.width(32)) PipelineINST (.D(multiplexer_1_out), .en(1'b1), .clk(clk), .Q(PINST));  // open: clr
  Register #(.width(32)) u_PipelinePC (.D(PROGRAM_COUNTER), .en(1'b1), .clk(clk), .Q(PipelinePC));  // open: clr
  Adder #(.width(32)) adder_1 (.a(PipelinePC), .b(32'h4), .out(PC4));  // open: cin, cout
  Adder #(.width(32)) adder_2 (.a(PROGRAM_COUNTER), .b(32'h4), .out(adder_2_out));  // open: cin, cout
  Multiplexer #(.enable("false"), .width(32)) multiplexer_2 (
    .in0(adder_2_out), .in1(WRITE_ADDRESS), .out(multiplexer_2_out), .sel(PCSel));
  Multiplexer #(.enable("false"), .select(2), .width(32)) multiplexer_3 (
    .in0(ReadResult), .in1(WRITE_ADDRESS), .in2(PC4), .out(multiplexer_3_out), .sel(WBSel));  // open: in3
  Register #(.width(32)) PC (.D(multiplexer_2_out), .en(1'b1), .clk(clk), .Q(PROGRAM_COUNTER));  // open: clr
  Register #(.width(1)) PipelinePCSel (.D(PCSel), .en(1'b1), .clk(clk), .Q(LastPCSel));  // open: clr
  imm_gen imm_gen_1 (.inst(PINST), .ImmSel(control_logic_1_immsel), .imm(imm_gen_1_imm));
  control_logic control_logic_1 (
    .CSRWen(control_logic_1_csrwen), .PCSel(PCSel), .RegWEn(control_logic_1_regwen),
    .ImmSel(control_logic_1_immsel), .BrUn(control_logic_1_brun), .ASel(control_logic_1_asel),
    .BSel(control_logic_1_bsel), .ALUSel(control_logic_1_alusel), .MemRW(control_logic_1_memrw),
    .WBSel(WBSel), .CSRSel(control_logic_1_csrsel), .inst(PINST), .BrEq(branch_comp_1_breq),
    .BrLt(branch_comp_1_brlt));
  regfile regfile_1 (
    .rs1(PINST[19:15]), .rs2(PINST[24:20]), .rd(PINST[11:7]), .Write_Data(multiplexer_3_out),
    .RegWEn(control_logic_1_regwen), .clk(clk), .ra(ra), .sp(sp), .t0(t0), .t1(t1), .t2(t2), .s0(s0),
    .s1(s1), .a0(a0), .Read_Data_1(rs1), .Read_Data_2(rs2));
  Register #(.width(32)) PipelineALU (.D(WRITE_ADDRESS), .en(1'b1), .clk(clk), .Q(LastALUResult));  // open: clr
  branch_comp branch_comp_1 (
    .rs1(rs1), .rs2(rs2), .BrUn(control_logic_1_brun), .BrEq(branch_comp_1_breq), .BrLt(branch_comp_1_brlt));
  Multiplexer #(.enable("false"), .width(32)) multiplexer_4 (
    .in0(rs1), .in1(imm_gen_1_imm), .out(multiplexer_4_out), .sel(control_logic_1_csrsel));
  Multiplexer #(.enable("false"), .width(32)) multiplexer_5 (
    .in0(rs1), .in1(PipelinePC), .out(multiplexer_5_out), .sel(control_logic_1_asel));
  Multiplexer #(.enable("false"), .width(32)) multiplexer_6 (
    .in0(rs2), .in1(imm_gen_1_imm), .out(multiplexer_6_out), .sel(control_logic_1_bsel));
  alu alu_1 (.Result(WRITE_ADDRESS), .A(multiplexer_5_out), .B(multiplexer_6_out), .ALUSel(control_logic_1_alusel));
  Multiplexer #(.enable("false"), .select(2), .width(4)) multiplexer_7 (
    .in0(4'b0001), .in1(4'b0011), .in2(4'b1111), .out(multiplexer_7_out), .sel(PINST[13:12]));  // open: in3
  // csr csr_1: pin names not known; wires that end beside it: PINST[31:20], multiplexer_4_out, control_logic_1_csrwen, clk, tohost
  Shifter #(.width(4)) shifter_1 (.in(multiplexer_7_out), .\dist (WRITE_ADDRESS[1:0]), .out(shifter_1_out));
  Multiplexer #(.enable("false"), .width(4)) multiplexer_8 (
    .in0(4'b0000), .in1(shifter_1_out), .out(WRITE_ENABLE), .sel(control_logic_1_memrw));
  Multiplexer #(.enable("false"), .select(2), .width(16)) multiplexer_9 (
    .in0(READ_DATA[15:0]), .in1(READ_DATA[23:8]), .in2(READ_DATA[31:16]), .out(multiplexer_9_out),
    .sel(WRITE_ADDRESS[1:0]));  // open: in3
  Multiplexer #(.enable("false"), .select(2), .width(8)) multiplexer_10 (
    .in0(READ_DATA[7:0]), .in1(READ_DATA[15:8]), .in2(READ_DATA[23:16]), .in3(READ_DATA[31:24]),
    .out(multiplexer_10_out), .sel(WRITE_ADDRESS[1:0]));
  assign bit_extender_1_out = {{16{multiplexer_9_out[15]}}, multiplexer_9_out};  // Bit_Extender bit_extender_1
  assign bit_extender_2_out = {{24{multiplexer_10_out[7]}}, multiplexer_10_out};  // Bit_Extender bit_extender_2
  Multiplexer #(.enable("false"), .select(2), .width(32)) multiplexer_11 (
    .in0(bit_extender_2_out), .in1(bit_extender_1_out), .in2(READ_DATA), .out(ReadResult), .sel(PINST[13:12]));  // open: in3
  Shifter #(.width(32)) shifter_2 (.in(rs2), .\dist ({WRITE_ADDRESS[1:0], 3'b000}), .out(WRITE_DATA));

  // Other names for the same wires on the sheet: ALUResult[31:0] = WRITE_ADDRESS; rdb0[7:0] = READ_DATA[7:0];
  //   rdb01[15:0] = READ_DATA[15:0]; rdb1[7:0] = READ_DATA[15:8]; rdb12[15:0] = READ_DATA[23:8];
  //   rdb2[7:0] = READ_DATA[23:16]; rdb23[15:0] = READ_DATA[31:16]; rdb3[7:0] = READ_DATA[31:24]

  // Notes on the sheet:
  //   Output to IMEM
  //   IMEM (do **NOT** move this)
  //   Inputs from IMEM
  //   Inputs/Outputs for testing. Do **NOT** move these.
  //   Outputs To DMEM
  //   DMEM (do **NOT** move this)
  //   Inputs From DMEM
endmodule
