// Logisim project imm-gen.circ as structural Verilog: 1 circuit, main circuit imm_gen
module imm_gen (
  input  [31:0] inst,
  input  [2:0] ImmSel,
  output [31:0] imm
);

  wire [31:0] I, S, SB, UJ;

  assign I = {{20{inst[31]}}, inst[31:20]};  // Bit_Extender bit_extender_1
  assign S = {{20{inst[31]}}, {inst[31:25], inst[11:7]}};  // Bit_Extender bit_extender_2
  assign SB = {{19{inst[31]}}, {inst[31], inst[7], inst[30:25], inst[11:8], 1'b0}};  // Bit_Extender bit_extender_3
  assign UJ = {{11{inst[31]}}, {inst[31], inst[19:12], inst[20], inst[30:21], 1'b0}};  // Bit_Extender bit_extender_4
  Multiplexer #(.enable("false"), .select(3), .width(32)) multiplexer_1 (
    .in0({32{1'b0}}), .in1(I), .in2(S), .in3(SB), .in4({inst[31:12], {12{1'b0}}}), .in5(UJ),
    .in6({{27{1'b0}}, inst[19:15]}), .out(imm), .sel(ImmSel));  // open: in7

  // Other names for the same wires on the sheet: U[31:12] = inst[31:12]; CSR[4:0] = inst[19:15]

  // Notes on the sheet:
  //   INPUTS to your circuit
  //   None=0, I=1, S=2, SB=3, U=4, UJ=5, CSR=6
  //   DON'T CHANGE THE LOCATIONS OF THE INPUTS AND OUTPUTS!
  //   OUTPUT from your circuit
endmodule
