// Logisim project cpu-test_registers.circ as structural Verilog: 1 circuit, main circuit run_main
module run_main (
  output [31:0] ra,
  output [31:0] sp,
  output [31:0] t0,
  output [31:0] t1,
  output [31:0] t2,
  output [31:0] s0,
  output [31:0] s1,
  output [31:0] a0,
  output [31:0] Requested_Address,
  output [31:0] Requested_Instruction,
  output [15:0] Time_Step,
  output halt
);

  wire clk;

  Clock clock_1 (.out(clk));
  // Probe on Requested_Address
  // cpu_harness cpu_harness_1: pin names not known; wires that end beside it: Requested_Instruction, clk, Requested_Address, ra, sp, t0, t1, t2, s0, s1, a0
  ROM #(.addrWidth(14), .dataWidth(32)) rom_1 (.addr(Requested_Address[15:2]), .data(Requested_Instruction));
  // Probe on Requested_Instruction
  Counter #(.max('hffff), .width(16)) counter_1 (.clk(clk), .Q(Time_Step));  // open: clr, load, up, count, D, carry
  Comparator #(.width(16)) comparator_1 (.a(Time_Step), .b(16'h44), .eq(halt));  // open: gt, lt

  // Other names for the same wires on the sheet: INSTRUCTION[31:0] = Requested_Instruction;
  //   PROGRAM_COUNTER[31:0] = Requested_Address

  // Notes on the sheet:
  //   contents of rom_1 (hex, n*v repeats v):
  //   2A00013 293 2A00093 8293 2A00113 10293 2A00193 18293 2A00213 20293 2A00293 28293 2A00313 30293
  //   2A00393 38293 2A00413 40293 2A00413 40293 2A00493 48293 2A00513 50293 2A00593 58293 2A00613 60293
  //   2A00693 68293 2A00713 70293 2A00793 78293 2A00813 80293 2A00893 88293 2A00913 90293 2A00993 98293
  //   2A00A13 A0293 2A00A93 A8293 2A00B13 B0293 2A00B93 B8293 2A00C13 C0293 2A00C93 C8293 2A00D13 D0293
  //   2A00D93 D8293 2A00E13 E0293 2A00E93 E8293 2A00F13 F0293 2A00F93 F8293
  //   Instruction Memory
  //   Halts Execution After Constant # of Clock Cycles
  //   Constant
endmodule
